// Digital circuit Lab10.dig as structural Verilog
module Lab10 (
  input  [8:0] N,
  input  start,
  input  clock,
  input  reset,
  output done,
  output [7:0] displayout,
  output [15:0] clockcount,
  output valid,
  output [7:0] out_8,
  output [7:0] out_9,
  output [7:0] out_10,
  output [7:0] out_11,
  output [8:0] out_12,
  output [8:0] out_13,
  output [8:0] out_14
);

  wire and_1_out, and_2_out, and_3_out, and_4_out, and_7_out, comparator_3_eq, comparator_4_eq,
       comparator_4_lt, comparator_5_eq, comparator_5_lt, comparator_6_eq, comparator_7_eq, d_ff_2_q,
       End_count, or_1_out, or_2_out, or_3_out, or_4_out, or_5_out, or_6_out, or_7_out, RAM_busy, ROM_busy,
       start_t;
  wire [7:0] multiplexer_1_out, multiplexer_2_out, multiplexer_3_out, multiplexer_4_out, multiplexer_5_out,
       multiplexer_7_out, multiplexer_10_out, ROM_data;
  wire [8:0] add_1_s, Disp_add, Loop, multiplexer_9_out, ROM_add, sub_1_s, sub_2_s;

  or or_1 (or_1_out, start, reset);
  and and_1 (and_1_out, RAM_busy, End_count);
  Register register_1 (.D(start), .C(clock), .en(or_1_out), .Q(start_t));
  Counter #(.Bits(9)) counter_1 (.en(and_1_out), .C(clock), .clr(reset), .out(Loop));  // open: ovf
  and and_2 (and_2_out, ~ROM_busy, ~End_count);  // And
  or or_2 (or_2_out, End_count, ~start_t, reset);  // Or
  and and_3 (and_3_out, ROM_busy, start_t);
  Counter #(.Bits(9)) counter_2 (.en(and_2_out), .C(clock), .clr(or_2_out), .out(out_14));  // open: ovf
  Sub #(.Bits(9)) sub_1 (.a(N), .b(Loop), .c_i(1'b1), .s(sub_1_s));  // open: c_o
  Add #(.Bits(9)) add_1 (.a(Loop), .b(9'h1), .c_i(1'b0), .s(add_1_s));  // open: c_o
  Comparator #(.Bits(9)) comparator_1 (.a(out_14), .b(sub_1_s), .eq(End_count));  // open: gt, lt
  Counter #(.Bits(9)) counter_3 (.en(and_3_out), .C(clock), .clr(reset), .out(ROM_add));  // open: ovf
  Comparator #(.Bits(9)) comparator_2 (.a(N), .b(add_1_s), .gt(RAM_busy));  // open: eq, lt
  Comparator #(.Bits(9)) comparator_3 (.a(ROM_add), .b(N), .eq(comparator_3_eq));  // open: gt, lt
  ROM #(.bigEndian("true"), .AddrBits(9), .isProgramMemory("true"), .Bits(8)) ROMFILE (
    .A(ROM_add), .sel(ROM_busy), .D(ROM_data));
  not not_1 (ROM_busy, comparator_3_eq);
  Comparator #(.Bits(8)) comparator_4 (
    .a(displayout), .b(out_11), .eq(comparator_4_eq), .lt(comparator_4_lt));  // open: gt
  Comparator #(.Bits(8)) comparator_5 (.a(out_9), .b(out_11), .eq(comparator_5_eq), .lt(comparator_5_lt));  // open: gt
  or or_3 (or_3_out, comparator_4_eq, comparator_4_lt);
  or or_4 (or_4_out, comparator_5_eq, comparator_5_lt);
  Multiplexer #(.Bits(8)) multiplexer_1 (.sel(or_3_out), .in_0(out_11), .in_1(displayout), .out(multiplexer_1_out));
  Comparator #(.Bits(9)) comparator_6 (.a(out_14), .b({9{1'b0}}), .eq(comparator_6_eq));  // open: gt, lt
  Multiplexer #(.Bits(8)) multiplexer_2 (.sel(or_3_out), .in_0(displayout), .in_1(out_11), .out(multiplexer_2_out));
  Multiplexer #(.Bits(8)) multiplexer_3 (.sel(or_4_out), .in_0(out_11), .in_1(out_9), .out(multiplexer_3_out));
  Multiplexer #(.Bits(8)) multiplexer_4 (.sel(or_4_out), .in_0(out_9), .in_1(out_11), .out(multiplexer_4_out));
  Multiplexer #(.Bits(8)) multiplexer_5 (.sel(and_4_out), .in_0(out_8), .in_1(out_9), .out(multiplexer_5_out));
  and and_4 (and_4_out, End_count, RAM_busy);
  Multiplexer #(.Bits(8)) multiplexer_6 (
    .sel(comparator_6_eq), .in_0(multiplexer_3_out), .in_1(multiplexer_1_out), .out(out_8));
  Multiplexer #(.Bits(8)) multiplexer_7 (
    .sel(comparator_6_eq), .in_0(multiplexer_4_out), .in_1(multiplexer_2_out), .out(multiplexer_7_out));
  Multiplexer #(.Bits(9)) multiplexer_8 (.sel(or_5_out), .in_0(Disp_add), .in_1(multiplexer_9_out), .out(out_13));
  Multiplexer #(.Bits(9)) multiplexer_9 (.sel(ROM_busy), .in_0(out_14), .in_1(ROM_add), .out(multiplexer_9_out));
  Multiplexer #(.Bits(8)) multiplexer_10 (
    .sel(ROM_busy), .in_0(multiplexer_5_out), .in_1(ROM_data), .out(multiplexer_10_out));
  or or_5 (or_5_out, ROM_busy, RAM_busy);
  D_FF #(.Bits(8)) d_ff_1 (.D(multiplexer_7_out), .C(clock), .Q(out_9));  // open: nQ
  Add #(.Bits(9)) add_2 (.a(out_13), .b(9'h1), .c_i(1'b0), .s(out_12));  // open: c_o
  D_FF d_ff_2 (.D(or_6_out), .C(clock), .Q(d_ff_2_q));  // open: nQ
  or or_6 (or_6_out, ROM_busy, RAM_busy);
  RAMDualAccess #(.AddrBits(9), .Bits(8)) ramdualaccess_1 (
    .str(d_ff_2_q), .C(clock), .ld(1'b1), .A1(out_13), .Din1(multiplexer_10_out), .A2(out_12),
    .D1(displayout), .D2(out_11));
  or or_7 (or_7_out, reset, ~start_t);  // Or
  Counter #(.Bits(9)) counter_4 (.en(valid), .C(clock), .clr(or_7_out), .out(Disp_add));  // open: ovf
  Sub #(.Bits(9)) sub_2 (.a(N), .b(9'h1), .c_i(1'b0), .s(sub_2_s));  // open: c_o
  Comparator #(.Bits(9)) comparator_7 (.a(Disp_add), .b(sub_2_s), .eq(comparator_7_eq));  // open: gt, lt
  and and_5 (valid, ~comparator_7_eq, ~ROM_busy, ~RAM_busy);  // And
  Seven_Seg_Hex seven_seg_hex_1 (.d(displayout[7:4]), .dp(1'b0));
  and and_6 (done, ~ROM_busy, ~valid, ~RAM_busy);  // And
  Seven_Seg_Hex seven_seg_hex_2 (.d(displayout[3:0]), .dp(1'b0));
  and and_7 (and_7_out, ~done, start_t);  // And
  Counter #(.Bits(16)) counter_5 (.en(and_7_out), .C(clock), .clr(reset), .out(clockcount));  // open: ovf

  assign out_10 = displayout;

  // Other names for the same wires on the sheet: clk = clock; D_1[7:0] = displayout; D_2[7:0] = out_11;
  //   Din_1[7:0] = out_8; Disp_busy = valid; QD_2[7:0] = out_9; RAM_add[8:0] = out_14

  // Notes on the sheet:
  //   clock: Hz: 10
  //   Sort - Bubble Sort
  //   Outer Loop
  //   Inner Loop
  //   Extracting ROM data
  //   ROMFILE loads t0.txt
  //   Swapper
  //   RAM handler
  //   Display address
endmodule
