// Digital circuit Lab10_2.dig as structural Verilog
module Lab10_2 (
  input  [8:0] N,
  input  reset,
  input  start,
  input  clock,
  output [7:0] displayout,
  output valid,
  output done,
  output [15:0] clockcount
);

  wire and_1_out, and_4_out, and_6_out, comparator_1_eq, comparator_2_eq, comparator_2_gt, comparator_3_eq,
       Extract_ROM, not_1_out, not_3_out, or_1_out, or_2_out, or_3_out, ROM_busy, Sorting;
  wire [7:0] add_2_s, multiplexer_2_out, multiplexer_3_out, multiplexer_6_out, ROM_data, Sort_add;
  wire [8:0] add_1_s, add_3_s, counter_1_out, Cur_add, multiplexer_1_out, multiplexer_4_out, RAM_data,
       Sort_data, sub_1_s;

  Comparator #(.Bits(9)) comparator_1 (.a(Cur_add), .b(N), .eq(comparator_1_eq));  // open: gt, lt
  not not_1 (not_1_out, comparator_1_eq);
  Counter #(.Bits(9)) counter_1 (.en(Extract_ROM), .C(clock), .clr(reset), .out(counter_1_out));  // open: ovf
  Add #(.Bits(9)) add_1 (.a(Cur_add), .b(9'h1), .c_i(1'b0), .s(add_1_s));  // open: c_o
  and and_1 (and_1_out, Sorting, valid, not_1_out);
  and and_2 (Extract_ROM, ROM_busy, start);
  Comparator #(.Bits(9)) comparator_2 (
    .a(RAM_data), .b({9{1'b0}}), .gt(comparator_2_gt), .eq(comparator_2_eq));  // open: lt
  Multiplexer #(.Bits(9)) multiplexer_1 (.sel(reset), .in_0(add_1_s), .in_1({9{1'b0}}), .out(multiplexer_1_out));
  or or_1 (or_1_out, and_1_out, reset);
  and and_3 (Sorting, ~Extract_ROM, not_1_out, start);  // And
  Comparator #(.Bits(9)) comparator_3 (.a(counter_1_out), .b(N), .eq(comparator_3_eq));  // open: gt, lt
  not not_2 (ROM_busy, comparator_3_eq);
  and and_4 (and_4_out, ~valid, Sorting);  // And
  Multiplexer #(.Bits(8)) multiplexer_2 (.sel(comparator_2_eq), .in_0({8{1'b0}}), .in_1(8'h1), .out(multiplexer_2_out));
  ROM #(.bigEndian("true"), .AddrBits(9), .isProgramMemory("true"), .Bits(8)) ROMFILE (
    .A(counter_1_out), .sel(ROM_busy), .D(ROM_data));
  Counter #(.Bits(8)) counter_2 (.en(and_4_out), .C(clock), .clr(reset), .out(Sort_add));  // open: ovf
  Add #(.Bits(8)) add_2 (.a(displayout), .b(multiplexer_2_out), .c_i(1'b0), .s(add_2_s));  // open: c_o
  and and_5 (valid, comparator_2_gt, Sorting);
  Register #(.Bits(9)) register_1 (.D(multiplexer_1_out), .C(clock), .en(or_1_out), .Q(Cur_add));
  Add #(.Bits(9)) add_3 (.a(RAM_data), .b(9'h1), .c_i(1'b0), .s(add_3_s));  // open: c_o
  Multiplexer #(.Bits(8)) multiplexer_3 (.sel(reset), .in_0(add_2_s), .in_1({8{1'b0}}), .out(multiplexer_3_out));
  or or_2 (or_2_out, Sorting, reset);
  Register #(.Bits(8)) CurrentNum (.D(multiplexer_3_out), .C(clock), .en(or_2_out), .Q(displayout));
  Sub #(.Bits(9)) sub_1 (.a(RAM_data), .b(9'h1), .c_i(1'b0), .s(sub_1_s));  // open: c_o
  Multiplexer #(.Bits(9)) multiplexer_4 (.sel(Sorting), .in_0(add_3_s), .in_1(Sort_data), .out(multiplexer_4_out));
  Multiplexer #(.Bits(9)) multiplexer_5 (.sel(not_3_out), .in_0(sub_1_s), .in_1(RAM_data), .out(Sort_data));
  not not_3 (not_3_out, valid);
  Multiplexer #(.Bits(8)) multiplexer_6 (.sel(Sorting), .in_0(ROM_data), .in_1(Sort_add), .out(multiplexer_6_out));
  or or_3 (or_3_out, Extract_ROM, Sorting);
  RAMDualPort #(.AddrBits(8), .Bits(9)) Sort_RAM (
    .A(multiplexer_6_out), .Din(multiplexer_4_out), .str(or_3_out), .C(clock), .ld(or_3_out), .D(RAM_data));
  nor nor_1 (done, Sorting, Extract_ROM, ROM_busy);
  Seven_Seg_Hex seven_seg_hex_1 (.d(displayout[7:4]), .dp(1'b0));
  Seven_Seg_Hex seven_seg_hex_2 (.d(displayout[3:0]), .dp(1'b0));
  and and_6 (and_6_out, ~done, start);  // And
  Counter #(.Bits(16)) counter_3 (.en(and_6_out), .C(clock), .clr(reset), .out(clockcount));  // open: ovf

  // Other names for the same wires on the sheet: clk = clock; Cur_num[7:0] = displayout; str = valid

  // Notes on the sheet:
  //   clock: Hz: 5
  //   contents of ROMFILE (hex, n*v repeats v):
  //   ff,2,3
endmodule
